// Logisim project 4_addersub.circ as structural Verilog: 5 circuits, main circuit main
module main (
  input  A,
  input  B,
  input  [2:0] A_valuee,
  input  [2:0] B_value,
  input  in_5,
  output [2:0] out_6
);

  wire Adder_out_5, decoder_1_a_2, decoder_1_b_2, decoder_1_c_2, decoder_1_d, decoder_1_e, decoder_1_f,
       decoder_1_g, multiplexer_1_out, Subtractor_out_5;
  wire [2:0] Adder_out_6, Subtractor_out_6;

  adder Adder (
    .Sign_bit_of_A(A), .Sign_bit_of_B(B), .in_3(A_valuee), .in_4(B_value), .out_5(Adder_out_5),
    .out_6(Adder_out_6));
  sub Subtractor (
    .Sign_bit_of_A(A), .Sign_bit_of_B(B), .in_3(A_valuee), .in_4(B_value), .out_5(Subtractor_out_5),
    .out_6(Subtractor_out_6));
  Multiplexer multiplexer_1 (
    .in0(Adder_out_5), .in1(Subtractor_out_5), .out(multiplexer_1_out), .sel(in_5));  // open: en
  _7_Segment_Display u_7_segment_display_1 (
    .g(decoder_1_g), .f(decoder_1_f), .a(decoder_1_a_2), .b(decoder_1_b_2), .e(decoder_1_e), .d(decoder_1_d),
    .c(decoder_1_c_2));  // open: dp
  _7_Segment_Display u_7_segment_display_2 (.g(multiplexer_1_out));  // open: f, a, b, e, d, c, dp
  Multiplexer #(.width(3)) multiplexer_2 (
    .in0(Adder_out_6), .in1(Subtractor_out_6), .out(out_6), .sel(in_5));  // open: en
  decoder decoder_1 (
    .A(out_6[2]), .B(out_6[1]), .C(out_6[0]), .a_2(decoder_1_a_2), .b_2(decoder_1_b_2), .c_2(decoder_1_c_2),
    .d(decoder_1_d), .e(decoder_1_e), .f(decoder_1_f), .g(decoder_1_g));

  // Notes on the sheet:
  //   default - sign
  //   default addition
  //   addition/substraction
  //   sign bit
endmodule

module adder (
  input  Sign_bit_of_A,
  input  Sign_bit_of_B,
  input  [2:0] in_3,
  input  [2:0] in_4,
  output out_5,
  output [2:0] out_6
);

  wire comparator_1_gt, comparator_1_lt, multiplexer_3_out, subtractor_1_bout, xor_1_out, xor_2_out,
       xor_3_out;
  wire [2:0] adder_1_out, multiplexer_1_out, n2_s_compliment_1_out_2, subtractor_1_out;

  xor xor_1 (xor_1_out, Sign_bit_of_A, Sign_bit_of_B);
  Subtractor #(.width(3)) subtractor_1 (
    .a(in_3), .b(in_4), .out(subtractor_1_out), .bout(subtractor_1_bout));  // open: bin
  Adder #(.width(3)) adder_1 (.a(in_3), .b(in_4), .out(adder_1_out));  // open: cin, cout
  _2_s_compliment u_2_s_compliment_1 (.in_1(subtractor_1_out), .out_2(n2_s_compliment_1_out_2));
  Comparator #(.width(3)) comparator_1 (.a(in_3), .b(in_4), .gt(comparator_1_gt), .lt(comparator_1_lt));  // open: eq
  Multiplexer #(.width(3)) multiplexer_1 (
    .in0(subtractor_1_out), .in1(n2_s_compliment_1_out_2), .out(multiplexer_1_out), .sel(subtractor_1_bout));  // open: en
  Multiplexer #(.width(3)) multiplexer_2 (
    .in0(adder_1_out), .in1(multiplexer_1_out), .out(out_6), .sel(xor_1_out));  // open: en
  xor xor_2 (xor_2_out, Sign_bit_of_A, comparator_1_gt);
  xor xor_3 (xor_3_out, Sign_bit_of_B, comparator_1_lt);
  Multiplexer multiplexer_3 (
    .in0(xor_2_out), .in1(xor_3_out), .out(multiplexer_3_out), .sel(comparator_1_lt));  // open: en
  not not_1 (out_5, multiplexer_3_out);

  // Notes on the sheet:
  //   -1--2
endmodule

module sub (
  input  Sign_bit_of_A,
  input  Sign_bit_of_B,
  input  [2:0] in_3,
  input  [2:0] in_4,
  output out_5,
  output [2:0] out_6
);

  wire comparator_1_gt, comparator_1_lt, multiplexer_3_out, subtractor_1_bout, xor_1_out, xor_2_out,
       xor_3_out;
  wire [2:0] adder_1_out, multiplexer_1_out, n2_s_compliment_1_out_2, subtractor_1_out;

  xor xor_1 (xor_1_out, Sign_bit_of_A, Sign_bit_of_B);
  Subtractor #(.width(3)) subtractor_1 (
    .a(in_3), .b(in_4), .out(subtractor_1_out), .bout(subtractor_1_bout));  // open: bin
  Adder #(.width(3)) adder_1 (.a(in_3), .b(in_4), .out(adder_1_out));  // open: cin, cout
  _2_s_compliment u_2_s_compliment_1 (.in_1(subtractor_1_out), .out_2(n2_s_compliment_1_out_2));
  Comparator #(.width(3)) comparator_1 (.a(in_3), .b(in_4), .gt(comparator_1_gt), .lt(comparator_1_lt));  // open: eq
  Multiplexer #(.width(3)) multiplexer_1 (
    .in0(subtractor_1_out), .in1(n2_s_compliment_1_out_2), .out(multiplexer_1_out), .sel(subtractor_1_bout));  // open: en
  Multiplexer #(.width(3)) multiplexer_2 (
    .in0(multiplexer_1_out), .in1(adder_1_out), .out(out_6), .sel(xor_1_out));  // open: en
  xor xor_2 (xor_2_out, Sign_bit_of_A, comparator_1_gt);
  xor xor_3 (xor_3_out, Sign_bit_of_B, comparator_1_lt);
  Multiplexer multiplexer_3 (
    .in0(xor_2_out), .in1(xor_3_out), .out(multiplexer_3_out), .sel(comparator_1_lt));  // open: en
  not not_1 (out_5, multiplexer_3_out);

  // Notes on the sheet:
  //   -1--2
endmodule

module decoder (
  input  A,
  input  B,
  input  C,
  output a_2,
  output b_2,
  output c_2,
  output d,
  output e,
  output f,
  output g
);

  wire and_1_out, and_2_out, and_3_out, and_4_out, and_5_out, and_6_out, and_7_out, and_8_out, and_9_out,
       and_10_out, and_11_out, and_12_out, and_13_out, and_14_out, and_15_out, and_16_out, not_1_out,
       not_2_out, not_3_out, not_4_out, not_5_out, not_6_out, not_7_out, not_8_out, not_9_out, not_10_out,
       not_11_out, not_12_out, not_13_out, not_14_out, not_15_out, not_16_out, not_17_out, not_18_out,
       not_19_out, not_20_out, not_21_out;

  not not_1 (not_1_out, A);
  not not_2 (not_2_out, C);
  not not_3 (not_3_out, B);
  not not_4 (not_4_out, C);
  not not_5 (not_5_out, B);
  not not_6 (not_6_out, A);
  not not_7 (not_7_out, C);
  not not_8 (not_8_out, A);
  not not_9 (not_9_out, C);
  not not_10 (not_10_out, B);
  not not_11 (not_11_out, A);
  not not_12 (not_12_out, C);
  not not_13 (not_13_out, C);
  not not_14 (not_14_out, B);
  not not_15 (not_15_out, C);
  not not_16 (not_16_out, B);
  not not_17 (not_17_out, C);
  not not_18 (not_18_out, A);
  not not_19 (not_19_out, B);
  not not_20 (not_20_out, C);
  and and_1 (and_1_out, not_1_out, not_2_out);
  and and_2 (and_2_out, A, C);
  not not_21 (not_21_out, A);
  and and_3 (and_3_out, not_3_out, not_4_out);
  and and_4 (and_4_out, B, C);
  or or_1 (c_2, not_5_out, C, A);
  and and_5 (and_5_out, not_6_out, not_7_out);
  and and_6 (and_6_out, not_8_out, B);
  and and_7 (and_7_out, B, not_9_out);
  and and_8 (and_8_out, A, not_10_out, C);
  and and_9 (and_9_out, not_11_out, not_12_out);
  and and_10 (and_10_out, B, not_13_out);
  and and_11 (and_11_out, not_14_out, not_15_out);
  and and_12 (and_12_out, A, not_16_out);
  and and_13 (and_13_out, A, not_17_out);
  and and_14 (and_14_out, not_18_out, B);
  and and_15 (and_15_out, A, not_19_out);
  and and_16 (and_16_out, A, not_20_out);
  or or_2 (a_2, and_1_out, B, and_2_out);
  or or_3 (b_2, not_21_out, and_3_out, and_4_out);
  or or_4 (d, and_5_out, and_6_out, and_7_out, and_8_out);
  or or_5 (e, and_9_out, and_10_out);
  or or_6 (f, and_11_out, and_12_out, and_13_out);
  or or_7 (g, and_14_out, and_15_out, and_16_out);
endmodule

module _2_s_compliment (
  input  [2:0] in_1,
  output [2:0] out_2
);

  wire [2:0] xor_1_out;

  assign xor_1_out = in_1 ^ 3'b111;  // XOR_Gate xor_1, 3 bits wide
  Adder #(.width(3)) adder_1 (.a(xor_1_out), .b(3'b000), .out(out_2), .cin(1'b1));  // open: cout
endmodule
